// Digital circuit ALU.dig as structural Verilog
module ALU (
  input  [7:0] b,
  input  Cin,
  input  [2:0] OP,
  input  [7:0] a,
  output [7:0] C,
  output Cout,
  output a_larger,
  output equal,
  output Zero,
  output M
);

  wire and_1_out, and_2_out, and_3_out, comparator_1_eq, comparator_1_gt, decoder_1_out_0, decoder_1_out_1,
       decoder_1_out_2, decoder_1_out_3, decoder_1_out_4, decoder_1_out_5, decoder_1_out_6, full_adder_1_c0,
       shift_lefter_1_sho, shift_right_1_sho;
  wire [7:0] andder_1_out, enable8_1_out, enable8_2_out, enable8_3_out, enable8_4_out, enable8_5_out,
       enable8_6_out, enable8_7_out, full_adder_1_o, not_1_out, orer_1_out, shift_lefter_1_o0,
       shift_right_1_o0, xorer_1_out;

  Comparator #(.Bits(8)) comparator_1 (.a(a), .b(b), .gt(comparator_1_gt), .eq(comparator_1_eq), .lt(M));
  assign not_1_out = ~a;  // Not not_1, 8 bits wide
  Shift_Right shift_right_1 (
    .ShI(Cin), .i0(a[0]), .i1(a[1]), .i2(a[2]), .i3(a[3]), .i4(a[4]), .i5(a[5]), .i6(a[6]), .i7(a[7]),
    .o0(shift_right_1_o0[0]), .o1(shift_right_1_o0[1]), .o2(shift_right_1_o0[2]), .o3(shift_right_1_o0[3]),
    .o4(shift_right_1_o0[4]), .o5(shift_right_1_o0[5]), .o6(shift_right_1_o0[6]), .o7(shift_right_1_o0[7]),
    .ShO(shift_right_1_sho));
  Shift_Lefter shift_lefter_1 (
    .ShO(shift_lefter_1_sho), .o0(shift_lefter_1_o0[0]), .o1(shift_lefter_1_o0[1]),
    .o2(shift_lefter_1_o0[2]), .o3(shift_lefter_1_o0[3]), .o4(shift_lefter_1_o0[4]),
    .o5(shift_lefter_1_o0[5]), .o6(shift_lefter_1_o0[6]), .o7(shift_lefter_1_o0[7]), .i0(a[0]), .i1(a[1]),
    .i2(a[2]), .i3(a[3]), .i4(a[4]), .i5(a[5]), .i6(a[6]), .i7(a[7]), .ShI(Cin));
  Full_adder full_adder_1 (
    .Cin(Cin), .i0(a[0]), .i1(a[1]), .i2(a[2]), .i3(a[3]), .i4(a[4]), .i5(a[5]), .i6(a[6]), .i7(a[7]),
    .b0(b[0]), .b1(b[1]), .b2(b[2]), .b3(b[3]), .b4(b[4]), .b5(b[5]), .b6(b[6]), .b7(b[7]),
    .O(full_adder_1_o), .C0(full_adder_1_c0));
  Andder andder_1 (
    .i0(a[0]), .i1(a[1]), .i2(a[2]), .i3(a[3]), .i4(a[4]), .i5(a[5]), .i6(a[6]), .i7(a[7]), .b0(b[0]),
    .b1(b[1]), .b2(b[2]), .b3(b[3]), .b4(b[4]), .b5(b[5]), .b6(b[6]), .b7(b[7]), .Out(andder_1_out));
  ORer orer_1 (
    .i0(a[0]), .i1(a[1]), .i2(a[2]), .i3(a[3]), .i4(a[4]), .i5(a[5]), .i6(a[6]), .i7(a[7]), .b0(b[0]),
    .b1(b[1]), .b2(b[2]), .b3(b[3]), .b4(b[4]), .b5(b[5]), .b6(b[6]), .b7(b[7]), .Out(orer_1_out));
  Decoder #(.Selector_Bits(3)) decoder_1 (
    .sel(OP), .out_0(decoder_1_out_0), .out_1(decoder_1_out_1), .out_2(decoder_1_out_2),
    .out_3(decoder_1_out_3), .out_4(decoder_1_out_4), .out_5(decoder_1_out_5), .out_6(decoder_1_out_6));  // open: out_7
  XORer xorer_1 (
    .i0(b[0]), .i1(b[1]), .i2(b[2]), .i3(b[3]), .i4(b[4]), .i5(b[5]), .i6(b[6]), .i7(b[7]), .b0(a[0]),
    .b1(a[1]), .b2(a[2]), .b3(a[3]), .b4(a[4]), .b5(a[5]), .b6(a[6]), .b7(a[7]), .Out(xorer_1_out));
  Enable8 enable8_1 (.A(andder_1_out), .E(decoder_1_out_4), .Out(enable8_1_out));
  Enable8 enable8_2 (.A(not_1_out), .E(decoder_1_out_3), .Out(enable8_2_out));
  Enable8 enable8_3 (.A(shift_right_1_o0), .E(decoder_1_out_1), .Out(enable8_3_out));
  and and_1 (and_1_out, shift_lefter_1_sho, decoder_1_out_2);
  Enable8 enable8_4 (.A(shift_lefter_1_o0), .E(decoder_1_out_2), .Out(enable8_4_out));
  and and_2 (and_2_out, full_adder_1_c0, decoder_1_out_0);
  Enable8 enable8_5 (.A(xorer_1_out), .E(decoder_1_out_6), .Out(enable8_5_out));
  Enable8 enable8_6 (.A(orer_1_out), .E(decoder_1_out_5), .Out(enable8_6_out));
  assign C = decoder_1_out_4 ? enable8_1_out : 8'bz;  // Driver driver_1
  Enable8 enable8_7 (.A(full_adder_1_o), .E(decoder_1_out_0), .Out(enable8_7_out));
  assign C = decoder_1_out_6 ? enable8_5_out : 8'bz;  // Driver driver_2
  assign C = decoder_1_out_5 ? enable8_6_out : 8'bz;  // Driver driver_3
  assign C = decoder_1_out_3 ? enable8_2_out : 8'bz;  // Driver driver_4
  assign C = decoder_1_out_1 ? enable8_3_out : 8'bz;  // Driver driver_5
  assign Cout = decoder_1_out_2 ? and_1_out : 1'bz;  // Driver driver_6
  assign C = decoder_1_out_2 ? enable8_4_out : 8'bz;  // Driver driver_7
  assign C = decoder_1_out_0 ? enable8_7_out : 8'bz;  // Driver driver_8
  and and_3 (and_3_out, shift_right_1_sho, decoder_1_out_1);
  Z z_1 (.a(C), .O(Zero));
  assign Cout = decoder_1_out_0 ? and_2_out : 1'bz;  // Driver driver_9
  assign Cout = decoder_1_out_1 ? and_3_out : 1'bz;  // Driver driver_10
  and and_4 (a_larger, comparator_1_gt, decoder_1_out_6);
  and and_5 (equal, comparator_1_eq, decoder_1_out_6);
endmodule
