// Digital circuit Andder.dig as structural Verilog
module Andder (
  input  i0,
  input  i1,
  input  i2,
  input  i3,
  input  i4,
  input  i5,
  input  i6,
  input  i7,
  input  b0,
  input  b1,
  input  b2,
  input  b3,
  input  b4,
  input  b5,
  input  b6,
  input  b7,
  output [7:0] Out
);

  assign Out = {i7, i6, i5, i4, i3, i2, i1, i0} & {b7, b6, b5, b4, b3, b2, b1, b0};  // And and_1, 8 bits wide
endmodule
