// Digital circuit Busone.dig as structural Verilog
module Busone (
  input  [7:0] in,
  input  Bus1,
  output [7:0] Bout
);

  wire not_1_out;

  not not_1 (not_1_out, Bus1);
  or or_1 (Bout[0], in[0], Bus1);
  and and_1 (Bout[1], in[1], not_1_out);
  and and_2 (Bout[2], in[2], not_1_out);
  and and_3 (Bout[3], in[3], not_1_out);
  and and_4 (Bout[4], in[4], not_1_out);
  and and_5 (Bout[5], in[5], not_1_out);
  and and_6 (Bout[6], in[6], not_1_out);
  and and_7 (Bout[7], in[7], not_1_out);
endmodule
