// Digital circuit Byte.dig as structural Verilog
module Byte (
  input  i0,
  input  i1,
  input  i2,
  input  i3,
  input  i4,
  input  i5,
  input  i6,
  input  i7,
  input  S,
  output A0,
  output A1,
  output A2,
  output A3,
  output A4,
  output A5,
  output A6,
  output A7
);

  Mlock mlock_1 (.c(i0), .S(S), .O(A0));
  Mlock mlock_2 (.c(i1), .S(S), .O(A1));
  Mlock mlock_3 (.c(i2), .S(S), .O(A2));
  Mlock mlock_4 (.c(i3), .S(S), .O(A3));
  Mlock mlock_5 (.c(i4), .S(S), .O(A4));
  Mlock mlock_6 (.c(i5), .S(S), .O(A5));
  Mlock mlock_7 (.c(i6), .S(S), .O(A6));
  Mlock mlock_8 (.c(i7), .S(S), .O(A7));
endmodule
