// Digital circuit COMPUTADORWITHOUTSTEPPER.dig as structural Verilog
module COMPUTADORWITHOUTSTEPPER (
  input  in_1,
  input  in_2,
  input  in_3,
  input  in_4,
  input  in_5,
  input  in_6,
  input  in_7,
  input  in_8,
  input  in_9,
  input  in_10,
  input  in_11,
  input  in_12,
  input  in_13,
  input  Eram,
  input  Sd,
  input  in_16
);

  wire [7:0] alu_1_p1, busone_1_bout, driver_1_out, mar_1_aout, ram_1_p5, register_1_o0, register_2_o0,
       register_3_o0, register_4_o0, register_5_o0, register_6_o0;

  Register register_1 (
    .i0(alu_1_p1[0]), .i1(alu_1_p1[1]), .i2(alu_1_p1[2]), .i3(alu_1_p1[3]), .i4(alu_1_p1[4]),
    .i5(alu_1_p1[5]), .i6(alu_1_p1[6]), .i7(alu_1_p1[7]), .S(in_12), .E(in_13), .o0(register_1_o0[0]),
    .o1(register_1_o0[1]), .o2(register_1_o0[2]), .o3(register_1_o0[3]), .o4(register_1_o0[4]),
    .o5(register_1_o0[5]), .o6(register_1_o0[6]), .o7(register_1_o0[7]));
  Busone busone_1 (.Bus1(in_16), .in(register_2_o0), .Bout(busone_1_bout));
  assign driver_1_out = in_13 ? register_1_o0 : 8'bz;  // Driver driver_1
  // ALU alu_1: pin names not known; wires that end beside it: alu_1_p1, busone_1_bout, driver_1_out
  Register register_2 (
    .i0(driver_1_out[0]), .i1(driver_1_out[1]), .i2(driver_1_out[2]), .i3(driver_1_out[3]),
    .i4(driver_1_out[4]), .i5(driver_1_out[5]), .i6(driver_1_out[6]), .i7(driver_1_out[7]), .S(in_11),
    .E(1'b1), .o0(register_2_o0[0]), .o1(register_2_o0[1]), .o2(register_2_o0[2]), .o3(register_2_o0[3]),
    .o4(register_2_o0[4]), .o5(register_2_o0[5]), .o6(register_2_o0[6]), .o7(register_2_o0[7]));
  Register register_3 (
    .i0(driver_1_out[0]), .i1(driver_1_out[1]), .i2(driver_1_out[2]), .i3(driver_1_out[3]),
    .i4(driver_1_out[4]), .i5(driver_1_out[5]), .i6(driver_1_out[6]), .i7(driver_1_out[7]), .S(in_1),
    .E(in_2), .o0(register_3_o0[0]), .o1(register_3_o0[1]), .o2(register_3_o0[2]), .o3(register_3_o0[3]),
    .o4(register_3_o0[4]), .o5(register_3_o0[5]), .o6(register_3_o0[6]), .o7(register_3_o0[7]));
  assign driver_1_out = in_2 ? register_3_o0 : 8'bz;  // Driver driver_2
  Register register_4 (
    .i0(driver_1_out[0]), .i1(driver_1_out[1]), .i2(driver_1_out[2]), .i3(driver_1_out[3]),
    .i4(driver_1_out[4]), .i5(driver_1_out[5]), .i6(driver_1_out[6]), .i7(driver_1_out[7]), .S(in_3),
    .E(in_4), .o0(register_4_o0[0]), .o1(register_4_o0[1]), .o2(register_4_o0[2]), .o3(register_4_o0[3]),
    .o4(register_4_o0[4]), .o5(register_4_o0[5]), .o6(register_4_o0[6]), .o7(register_4_o0[7]));
  assign driver_1_out = in_4 ? register_4_o0 : 8'bz;  // Driver driver_3
  Register register_5 (
    .i0(driver_1_out[0]), .i1(driver_1_out[1]), .i2(driver_1_out[2]), .i3(driver_1_out[3]),
    .i4(driver_1_out[4]), .i5(driver_1_out[5]), .i6(driver_1_out[6]), .i7(driver_1_out[7]), .S(in_5),
    .E(in_6), .o0(register_5_o0[0]), .o1(register_5_o0[1]), .o2(register_5_o0[2]), .o3(register_5_o0[3]),
    .o4(register_5_o0[4]), .o5(register_5_o0[5]), .o6(register_5_o0[6]), .o7(register_5_o0[7]));
  assign driver_1_out = in_6 ? register_5_o0 : 8'bz;  // Driver driver_4
  Register register_6 (
    .i0(driver_1_out[0]), .i1(driver_1_out[1]), .i2(driver_1_out[2]), .i3(driver_1_out[3]),
    .i4(driver_1_out[4]), .i5(driver_1_out[5]), .i6(driver_1_out[6]), .i7(driver_1_out[7]), .S(in_7),
    .E(in_8), .o0(register_6_o0[0]), .o1(register_6_o0[1]), .o2(register_6_o0[2]), .o3(register_6_o0[3]),
    .o4(register_6_o0[4]), .o5(register_6_o0[5]), .o6(register_6_o0[6]), .o7(register_6_o0[7]));
  assign driver_1_out = in_8 ? register_6_o0 : 8'bz;  // Driver driver_5
  MAR mar_1 (
    .a0(driver_1_out[0]), .a1(driver_1_out[1]), .a2(driver_1_out[2]), .a3(driver_1_out[3]),
    .a4(driver_1_out[4]), .a5(driver_1_out[5]), .a6(driver_1_out[6]), .a7(driver_1_out[7]), .S(in_9),
    .E(in_10), .Aout(mar_1_aout));
  // Ram ram_1: pin names not known; wires that end beside it: driver_1_out, Sd, Eram, mar_1_aout, ram_1_p5
  assign driver_1_out = Eram ? ram_1_p5 : 8'bz;  // Driver driver_6
endmodule
