// Digital circuit CounterProgram.dig as structural Verilog
module CounterProgram (
  input  in_1,
  input  in_2,
  input  in_3,
  input  in_4,
  input  in_5,
  input  clk,
  input  clk_2,
  input  in_13,
  input  [2:0] in_14,
  output out_8,
  output out_9,
  output out_10,
  output out_11,
  output out_12,
  output [7:0] out_15
);

  wire and_1_out, and_2_out, and_3_out, and_4_out, and_5_out, and_6_out, and_7_out, and_8_out, and_9_out,
       clk_1_clk_e, clk_1_clk_s, stepper_count_1__1, stepper_count_1__2, stepper_count_1__3,
       stepper_count_1__4, stepper_count_1__5;
  wire [7:0] alu_1_c, driver_1_out, mar_1_aout, ramdualport_1_d, register_1_o0, register_2_o0, register_3_o0,
       register_4_o0, register_5_o0, register_6_o0;

  Register register_1 (
    .i0(alu_1_c[0]), .i1(alu_1_c[1]), .i2(alu_1_c[2]), .i3(alu_1_c[3]), .i4(alu_1_c[4]), .i5(alu_1_c[5]),
    .i6(alu_1_c[6]), .i7(alu_1_c[7]), .S(and_4_out), .E(and_3_out), .o0(register_1_o0[0]),
    .o1(register_1_o0[1]), .o2(register_1_o0[2]), .o3(register_1_o0[3]), .o4(register_1_o0[4]),
    .o5(register_1_o0[5]), .o6(register_1_o0[6]), .o7(register_1_o0[7]));
  Busone busone_1 (.Bus1(and_1_out), .in(register_2_o0), .Bout(out_15));
  assign driver_1_out = and_3_out ? register_1_o0 : 8'bz;  // Driver driver_1
  ALU alu_1 (
    .a(driver_1_out), .b(out_15), .Cin(in_13), .OP(in_14), .a_larger(out_8), .equal(out_9), .M(out_10),
    .Zero(out_11), .C(alu_1_c), .Cout(out_12));
  Register register_2 (
    .i0(driver_1_out[0]), .i1(driver_1_out[1]), .i2(driver_1_out[2]), .i3(driver_1_out[3]),
    .i4(driver_1_out[4]), .i5(driver_1_out[5]), .i6(driver_1_out[6]), .i7(driver_1_out[7]), .S(in_5),
    .E(1'b1), .o0(register_2_o0[0]), .o1(register_2_o0[1]), .o2(register_2_o0[2]), .o3(register_2_o0[3]),
    .o4(register_2_o0[4]), .o5(register_2_o0[5]), .o6(register_2_o0[6]), .o7(register_2_o0[7]));
  and and_1 (and_1_out, clk_1_clk_s, stepper_count_1__2);
  clk clk_1 (.clk(clk), .clk_d(clk_2), .clk_e(clk_1_clk_e), .clk_s(clk_1_clk_s));
  and and_2 (and_2_out, clk_1_clk_e, stepper_count_1__2);
  and and_3 (and_3_out, stepper_count_1__3, clk_1_clk_e);
  Register register_3 (
    .i0(driver_1_out[0]), .i1(driver_1_out[1]), .i2(driver_1_out[2]), .i3(driver_1_out[3]),
    .i4(driver_1_out[4]), .i5(driver_1_out[5]), .i6(driver_1_out[6]), .i7(driver_1_out[7]), .S(and_6_out),
    .E(and_2_out), .o0(register_3_o0[0]), .o1(register_3_o0[1]), .o2(register_3_o0[2]),
    .o3(register_3_o0[3]), .o4(register_3_o0[4]), .o5(register_3_o0[5]), .o6(register_3_o0[6]),
    .o7(register_3_o0[7]));
  Stepper_count stepper_count_1 (
    .clk(clk), ._1(stepper_count_1__1), ._2(stepper_count_1__2), ._3(stepper_count_1__3),
    ._4(stepper_count_1__4), ._5(stepper_count_1__5));  // open: _6, _7
  and and_4 (and_4_out, stepper_count_1__2, clk_1_clk_s);
  assign driver_1_out = and_2_out ? register_3_o0 : 8'bz;  // Driver driver_2
  and and_5 (and_5_out, stepper_count_1__1, clk_1_clk_e);
  and and_6 (and_6_out, stepper_count_1__3, clk_1_clk_s);
  Register register_4 (
    .i0(driver_1_out[0]), .i1(driver_1_out[1]), .i2(driver_1_out[2]), .i3(driver_1_out[3]),
    .i4(driver_1_out[4]), .i5(driver_1_out[5]), .i6(driver_1_out[6]), .i7(driver_1_out[7]), .S(in_1),
    .E(and_5_out), .o0(register_4_o0[0]), .o1(register_4_o0[1]), .o2(register_4_o0[2]),
    .o3(register_4_o0[3]), .o4(register_4_o0[4]), .o5(register_4_o0[5]), .o6(register_4_o0[6]),
    .o7(register_4_o0[7]));
  assign driver_1_out = and_5_out ? register_4_o0 : 8'bz;  // Driver driver_3
  and and_7 (and_7_out, stepper_count_1__4, clk_1_clk_e);
  Register register_5 (
    .i0(driver_1_out[0]), .i1(driver_1_out[1]), .i2(driver_1_out[2]), .i3(driver_1_out[3]),
    .i4(driver_1_out[4]), .i5(driver_1_out[5]), .i6(driver_1_out[6]), .i7(driver_1_out[7]), .S(in_2),
    .E(and_7_out), .o0(register_5_o0[0]), .o1(register_5_o0[1]), .o2(register_5_o0[2]),
    .o3(register_5_o0[3]), .o4(register_5_o0[4]), .o5(register_5_o0[5]), .o6(register_5_o0[6]),
    .o7(register_5_o0[7]));
  assign driver_1_out = and_7_out ? register_5_o0 : 8'bz;  // Driver driver_4
  Register register_6 (
    .i0(driver_1_out[0]), .i1(driver_1_out[1]), .i2(driver_1_out[2]), .i3(driver_1_out[3]),
    .i4(driver_1_out[4]), .i5(driver_1_out[5]), .i6(driver_1_out[6]), .i7(driver_1_out[7]), .S(in_3),
    .E(in_4), .o0(register_6_o0[0]), .o1(register_6_o0[1]), .o2(register_6_o0[2]), .o3(register_6_o0[3]),
    .o4(register_6_o0[4]), .o5(register_6_o0[5]), .o6(register_6_o0[6]), .o7(register_6_o0[7]));
  assign driver_1_out = in_4 ? register_6_o0 : 8'bz;  // Driver driver_5
  and and_8 (and_8_out, stepper_count_1__1, clk_1_clk_s);
  and and_9 (and_9_out, stepper_count_1__2, clk_1_clk_s);
  MAR mar_1 (
    .a0(driver_1_out[0]), .a1(driver_1_out[1]), .a2(driver_1_out[2]), .a3(driver_1_out[3]),
    .a4(driver_1_out[4]), .a5(driver_1_out[5]), .a6(driver_1_out[6]), .a7(driver_1_out[7]), .S(and_8_out),
    .E(1'b1), .Aout(mar_1_aout));
  RAMDualPort #(.AddrBits(8), .Bits(8)) ramdualport_1 (
    .A(mar_1_aout), .Din(driver_1_out), .str(and_9_out), .C(and_9_out), .ld(stepper_count_1__5),
    .D(ramdualport_1_d));
  assign driver_1_out = stepper_count_1__5 ? ramdualport_1_d : 8'bz;  // Driver driver_6
endmodule
