// Digital circuit Decoder.dig as structural Verilog
module Decoder (
  input  [2:0] a,
  output o0,
  output o1,
  output o2,
  output o3,
  output o4,
  output o5,
  output o6,
  output o7
);

  Decoder #(.Selector_Bits(3)) decoder_1 (
    .sel(a), .out_0(o0), .out_1(o1), .out_2(o2), .out_3(o3), .out_4(o4), .out_5(o5), .out_6(o6), .out_7(o7));
endmodule
