// Digital circuit Enable.dig as structural Verilog
module Enable (
  input  a0,
  input  a1,
  input  a2,
  input  a3,
  input  a4,
  input  a5,
  input  a6,
  input  a7,
  input  E,
  output O0,
  output O1,
  output O2,
  output O3,
  output O4,
  output O5,
  output O6,
  output O7
);

  and and_1 (O0, a0, E);
  and and_2 (O1, a1, E);
  and and_3 (O2, a2, E);
  and and_4 (O3, a3, E);
  and and_5 (O4, a4, E);
  and and_6 (O5, a5, E);
  and and_7 (O6, a6, E);
  and and_8 (O7, a7, E);
endmodule
