// Digital circuit Enable8.dig as structural Verilog
module Enable8 (
  input  [7:0] A,
  input  E,
  output [7:0] Out
);

  and and_1 (Out[0], A[0], E);
  and and_2 (Out[1], A[1], E);
  and and_3 (Out[2], A[2], E);
  and and_4 (Out[3], A[3], E);
  and and_5 (Out[4], A[4], E);
  and and_6 (Out[5], A[5], E);
  and and_7 (Out[6], A[6], E);
  and and_8 (Out[7], A[7], E);
endmodule
