// Digital circuit Full adder.dig as structural Verilog
module Full_adder (
  input  Cin,
  input  i0,
  input  i1,
  input  i2,
  input  i3,
  input  i4,
  input  i5,
  input  i6,
  input  i7,
  input  b0,
  input  b1,
  input  b2,
  input  b3,
  input  b4,
  input  b5,
  input  b6,
  input  b7,
  output [7:0] O,
  output C0
);

  Add #(.Bits(8)) add_1 (
    .a({i7, i6, i5, i4, i3, i2, i1, i0}), .b({b7, b6, b5, b4, b3, b2, b1, b0}), .c_i(Cin), .s(O), .c_o(C0));
endmodule
