// Digital circuit MAR.dig as structural Verilog
module MAR (
  input  a0,
  input  a1,
  input  a2,
  input  a3,
  input  a4,
  input  a5,
  input  a6,
  input  a7,
  input  S,
  input  E,
  output [7:0] Aout
);

  Register register_1 (
    .i0(a0), .i1(a1), .i2(a2), .i3(a3), .i4(a4), .i5(a5), .i6(a6), .i7(a7), .S(S), .E(E), .o0(Aout[0]),
    .o1(Aout[1]), .o2(Aout[2]), .o3(Aout[3]), .o4(Aout[4]), .o5(Aout[5]), .o6(Aout[6]), .o7(Aout[7]));
endmodule
