// Digital circuit Mlock.dig as structural Verilog
module Mlock (
  input  c,
  input  S,
  output O
);

  wire nand_1_out, nand_2_out, nand_4_out, reset_1_out;

  nand nand_1 (nand_1_out, c, S);
  nand nand_2 (nand_2_out, nand_1_out, S);
  nand nand_3 (O, nand_1_out, nand_4_out);
  nand nand_4 (nand_4_out, O, reset_1_out, nand_2_out);
  Reset reset_1 (.out(reset_1_out));
endmodule
