// Digital circuit Register.dig as structural Verilog
module Register (
  input  i0,
  input  i1,
  input  i2,
  input  i3,
  input  i4,
  input  i5,
  input  i6,
  input  i7,
  input  S,
  input  E,
  output o0,
  output o1,
  output o2,
  output o3,
  output o4,
  output o5,
  output o6,
  output o7
);

  wire byte_1_a0, byte_1_a1, byte_1_a2, byte_1_a3, byte_1_a4, byte_1_a5, byte_1_a6, byte_1_a7;

  Byte byte_1 (
    .i0(i0), .i1(i1), .i2(i2), .i3(i3), .i4(i4), .i5(i5), .i6(i6), .i7(i7), .S(S), .A0(byte_1_a0),
    .A1(byte_1_a1), .A2(byte_1_a2), .A3(byte_1_a3), .A4(byte_1_a4), .A5(byte_1_a5), .A6(byte_1_a6),
    .A7(byte_1_a7));
  Enable enable_1 (
    .a0(byte_1_a0), .a1(byte_1_a1), .a2(byte_1_a2), .a3(byte_1_a3), .a4(byte_1_a4), .a5(byte_1_a5),
    .a6(byte_1_a6), .a7(byte_1_a7), .E(E), .O0(o0), .O1(o1), .O2(o2), .O3(o3), .O4(o4), .O5(o5), .O6(o6),
    .O7(o7));
endmodule
