// Digital circuit Shift Right.dig as structural Verilog
module Shift_Right (
  input  i0,
  input  i1,
  input  i2,
  input  i3,
  input  i5,
  input  i4,
  input  i6,
  input  i7,
  input  ShI,
  output o0,
  output o1,
  output o2,
  output o4,
  output o3,
  output o5,
  output o6,
  output o7,
  output ShO
);

  wire register_1_o0, register_1_o1, register_1_o2, register_1_o3, register_1_o4, register_1_o5,
       register_1_o6;

  Register register_1 (
    .i0(i0), .i1(i1), .i2(i2), .i3(i3), .i4(i4), .i5(i5), .i6(i6), .i7(i7), .S(1'b1), .E(1'b1),
    .o0(register_1_o0), .o1(register_1_o1), .o2(register_1_o2), .o3(register_1_o3), .o4(register_1_o4),
    .o5(register_1_o5), .o6(register_1_o6), .o7(ShO));
  Register register_2 (
    .i0(ShI), .i1(register_1_o0), .i2(register_1_o1), .i3(register_1_o2), .i4(register_1_o3),
    .i5(register_1_o4), .i6(register_1_o5), .i7(register_1_o6), .S(1'b1), .E(1'b1), .o0(o0), .o1(o1),
    .o2(o2), .o3(o3), .o4(o4), .o5(o5), .o6(o6), .o7(o7));
endmodule
