// Digital circuit Stepper count.dig as structural Verilog
module Stepper_count (
  input  clk,
  output _1,
  output _2,
  output _3,
  output _4,
  output _5,
  output _6,
  output _7
);

  wire d_ff_1_nq, mlock_1_o, mlock_2_o, mlock_3_o, mlock_4_o, mlock_5_o, mlock_6_o, mlock_7_o, mlock_8_o,
       mlock_9_o, mlock_10_o, mlock_11_o, not_1_out, not_2_out, not_3_out, not_4_out, not_5_out, not_6_out,
       not_7_out, not_8_out, or_1_out, or_2_out;

  D_FF d_ff_1 (.D(1'b1), .C(clk), .nQ(d_ff_1_nq));  // open: Q
  not not_1 (not_1_out, clk);
  not not_2 (not_2_out, d_ff_1_nq);
  or or_1 (or_1_out, d_ff_1_nq, not_1_out);
  or or_2 (or_2_out, d_ff_1_nq, clk);
  or or_3 (_1, d_ff_1_nq, not_3_out);
  Mlock mlock_1 (.c(not_2_out), .S(or_1_out), .O(mlock_1_o));
  not not_3 (not_3_out, mlock_2_o);
  Mlock mlock_2 (.c(mlock_1_o), .S(or_2_out), .O(mlock_2_o));
  and and_1 (_2, mlock_2_o, not_4_out);
  Mlock mlock_3 (.c(mlock_2_o), .S(or_1_out), .O(mlock_3_o));
  assign d_ff_1_nq = _7 ? _7 : 1'bz;  // Driver driver_1
  not not_4 (not_4_out, mlock_4_o);
  Mlock mlock_4 (.c(mlock_3_o), .S(or_2_out), .O(mlock_4_o));
  and and_2 (_3, mlock_4_o, not_5_out);
  Mlock mlock_5 (.c(mlock_4_o), .S(or_1_out), .O(mlock_5_o));
  Mlock mlock_6 (.c(mlock_5_o), .S(or_2_out), .O(mlock_6_o));
  not not_5 (not_5_out, mlock_6_o);
  and and_3 (_4, mlock_6_o, not_6_out);
  Mlock mlock_7 (.c(mlock_6_o), .S(or_1_out), .O(mlock_7_o));
  Mlock mlock_8 (.c(mlock_7_o), .S(or_2_out), .O(mlock_8_o));
  not not_6 (not_6_out, mlock_8_o);
  and and_4 (_5, mlock_8_o, not_7_out);
  Mlock mlock_9 (.c(mlock_8_o), .S(or_1_out), .O(mlock_9_o));
  not not_7 (not_7_out, mlock_10_o);
  Mlock mlock_10 (.c(mlock_9_o), .S(or_2_out), .O(mlock_10_o));
  Mlock mlock_11 (.c(mlock_10_o), .S(or_1_out), .O(mlock_11_o));
  and and_5 (_6, mlock_10_o, not_8_out);
  Mlock mlock_12 (.c(mlock_11_o), .S(or_2_out), .O(_7));
  not not_8 (not_8_out, _7);
endmodule
