// Digital circuit Z.dig as structural Verilog
module Z (
  input  [7:0] a,
  output O
);

  wire or_1_out, or_2_out, or_3_out;

  or or_1 (or_1_out, a[0], a[1], a[2], a[3]);
  or or_2 (or_2_out, a[4], a[5], a[6], a[7]);
  or or_3 (or_3_out, or_1_out, or_2_out);
  not not_1 (O, or_3_out);
endmodule
