// Digital circuit clk.dig as structural Verilog
module clk (
  input  clk,
  input  clk_d,
  output clk_e,
  output clk_s
);

  and and_1 (clk_s, clk, clk_d);
  or or_1 (clk_e, clk, clk_d);
endmodule
